# Fritzing sketch SchemaBranchements(10-02-23) (saved by Fritzing 0.9.3b)
breadboards: 1

parts:
  Amica_NodeMCU_DevKit_1_1 = Amica NodeMCU DevKit 1.0
  M1 = v.Kel GPS module

nets:
  N1: Amica_NodeMCU_DevKit_1_1.pin1, Amica_NodeMCU_DevKit_1_1.pin_10, M1.Pin_1, M1.Pin_5
  N2: Amica_NodeMCU_DevKit_1_1.pin2, Amica_NodeMCU_DevKit_1_1.pin_9, M1.Pin_2
  N3: Amica_NodeMCU_DevKit_1_1.pin6, M1.Pin_3
  N4: Amica_NodeMCU_DevKit_1_1.pin7, M1.Pin_4

custom parts:
  Amica NodeMCU DevKit 1.0: Amica NodeMCU DEVKIT 1.0 Development Kit based on ESP8266 ESP-12E, integating GPIO, PWM, IIC, 1-Wire and ADC all in one board.
  v.Kel GPS module: Generic v.Kel GPS module
