# Fritzing sketch SchemaBranchements(21-02-23) (saved by Fritzing 0.9.3b)
breadboards: 1

parts:
  Amica_NodeMCU_DevKit_1_1 = Amica NodeMCU DevKit 1.0
  M1 = v.Kel GPS module
  microSD1 = MicroSD Card Module

nets:
  N1: Amica_NodeMCU_DevKit_1_1.pin1, Amica_NodeMCU_DevKit_1_1.pin_10, microSD1.VCC
  N2: Amica_NodeMCU_DevKit_1_1.pin2, Amica_NodeMCU_DevKit_1_1.pin_9, microSD1.GND
  N3: Amica_NodeMCU_DevKit_1_1.pin5, microSD1.CS
  N4: Amica_NodeMCU_DevKit_1_1.pin6, microSD1.MOSI
  N5: Amica_NodeMCU_DevKit_1_1.pin7, microSD1.MISO
  N6: Amica_NodeMCU_DevKit_1_1.pin8, microSD1.SCK
  N7: Amica_NodeMCU_DevKit_1_1.pin_13, M1.Pin_4
  N8: Amica_NodeMCU_DevKit_1_1.pin_14, M1.Pin_3
  N9: M1.Pin_1, M1.Pin_5

custom parts:
  Amica NodeMCU DevKit 1.0: Amica NodeMCU DEVKIT 1.0 Development Kit based on ESP8266 ESP-12E, integating GPIO, PWM, IIC, 1-Wire and ADC all in one board.
  v.Kel GPS module: Generic v.Kel GPS module
