# Fritzing sketch SchemaBranchements(26-03-23) (saved by Fritzing 0.9.3b)
breadboards: 1

parts:
  Amica_NodeMCU_DevKit_1_1 = Amica NodeMCU DevKit 1.0
  M1 = v.Kel GPS module
  Squix1 = OLED 0.96" 128x64 I2C SSD1306
  SD_card_module2 = SD Card Module
  VCC1 = Battery

nets:
  N1: Amica_NodeMCU_DevKit_1_1.pin1, Amica_NodeMCU_DevKit_1_1.pin_10, Amica_NodeMCU_DevKit_1_1.pin_26
  N2: Amica_NodeMCU_DevKit_1_1.pin2, Amica_NodeMCU_DevKit_1_1.pin_9, Amica_NodeMCU_DevKit_1_1.pin_25, Amica_NodeMCU_DevKit_1_1.pin_29, M1.Pin_2, Squix1.GND, SD_card_module2.+5, VCC1.-
  N3: Amica_NodeMCU_DevKit_1_1.pin5, SD_card_module2.MISO
  N4: Amica_NodeMCU_DevKit_1_1.pin6, SD_card_module2.MOSI
  N5: Amica_NodeMCU_DevKit_1_1.pin7, SD_card_module2.SCK
  N6: Amica_NodeMCU_DevKit_1_1.pin8, SD_card_module2.CS
  N7: Amica_NodeMCU_DevKit_1_1.pin_11, M1.Pin_4
  N8: Amica_NodeMCU_DevKit_1_1.pin_12, M1.Pin_3
  N9: Amica_NodeMCU_DevKit_1_1.pin_13, Squix1.SCA
  N10: Amica_NodeMCU_DevKit_1_1.pin_14, Squix1.SCL
  N11: Amica_NodeMCU_DevKit_1_1.pin_30, M1.Pin_1, M1.Pin_5, Squix1.VCC, SD_card_module2.+3.3, VCC1.+

custom parts:
  Amica NodeMCU DevKit 1.0: Amica NodeMCU DEVKIT 1.0 Development Kit based on ESP8266 ESP-12E, integating GPIO, PWM, IIC, 1-Wire and ADC all in one board.
  v.Kel GPS module: Generic v.Kel GPS module
  SD Card Module: SD Card Module Slot Socket Reader For Arduino ARM MCU
